# Fritzing sketch kinotracker-fritzing (saved by Fritzing 0.8.5b)
circuit board: 8.46667cm x 5.64444cm
breadboards: 1

parts:
  Arduino_Nano = Arduino Nano (Rev3.0)
  wireless_link = female pin header, 4 pins [form="♀ (female)"]
  GPS_receiver = female pin header, 4 pins [form="♀ (female)"]

nets:
  N1: Arduino_Nano.D1/TX, wireless_link.pin3
  N2: Arduino_Nano.D0/RX, wireless_link.pin4
  GND: Arduino_Nano.GND, wireless_link.pin2, GPS_receiver.pin2
  N3: Arduino_Nano.D7, GPS_receiver.pin3
  N4: Arduino_Nano.D8, GPS_receiver.pin4
  N5: Arduino_Nano.5V, wireless_link.pin1, GPS_receiver.pin1
